// Logisim project processorsimulator.circ as structural Verilog: 10 circuits, main circuit 4bitcounter
// SC
module _4bitcounter (
  input  CLK,
  input  INC,
  input  clr,
  output [3:0] t
);

  wire and_1_out, and_2_out, and_3_out, and_4_out, and_5_out, and_6_out, and_7_out, not_1_out, xor_1_out,
       xor_2_out, xor_3_out, xor_4_out;

  and and_1 (and_1_out, t[0], INC);
  and and_2 (and_2_out, and_1_out, t[1]);
  and and_3 (and_3_out, and_2_out, t[2]);
  xor xor_1 (xor_1_out, t[0], INC);
  xor xor_2 (xor_2_out, and_1_out, t[1]);
  xor xor_3 (xor_3_out, and_2_out, t[2]);
  xor xor_4 (xor_4_out, and_3_out, t[3]);
  and and_4 (and_4_out, xor_1_out, not_1_out);
  and and_5 (and_5_out, xor_2_out, not_1_out);
  and and_6 (and_6_out, xor_3_out, not_1_out);
  and and_7 (and_7_out, xor_4_out, not_1_out);
  not not_1 (not_1_out, clr);
  D_Flip_Flop d_ff_1 (.clk(CLK), .D(and_4_out), .Q(t[0]));  // open: Qn, preset, en, reset
  D_Flip_Flop d_ff_2 (.clk(CLK), .D(and_5_out), .Q(t[1]));  // open: Qn, preset, en, reset
  D_Flip_Flop d_ff_3 (.clk(CLK), .D(and_6_out), .Q(t[2]));  // open: Qn, preset, en, reset
  D_Flip_Flop d_ff_4 (.clk(CLK), .D(and_7_out), .Q(t[3]));  // open: Qn, preset, en, reset
endmodule

// register
module _16_bit_register (
  input  [15:0] in_1,
  input  LOAD,
  input  CLR,
  input  CLK,
  input  INC,
  output [15:0] out_6
);

  wire and_1_out, and_2_out, and_3_out, and_4_out, and_5_out, and_6_out, and_7_out, and_8_out, and_9_out,
       and_10_out, and_11_out, and_12_out, and_13_out, and_14_out, and_15_out, and_16_out, and_17_out,
       and_18_out, and_19_out, and_20_out, and_21_out, and_22_out, and_23_out, and_24_out, and_25_out,
       and_26_out, and_27_out, and_28_out, and_29_out, and_30_out, and_31_out, and_32_out, and_33_out,
       and_34_out, and_35_out, and_36_out, inc_2_out, inc_3_out, inc_out, load0_2_out, load0_3_out,
       load0_4_out, load0_out, load1_2_out, load1_3_out, load1_4_out, load1_out, not_1_out, not_2_out,
       not_3_out, not_4_out, not_5_out, not_6_out, not_7_out, not_8_out, not_9_out, not_10_out, not_11_out,
       not_12_out, not_13_out, not_14_out, not_15_out, not_16_out, or_1_out, or_2_out, or_3_out, or_4_out,
       or_5_out, or_6_out, or_7_out, or_8_out, or_9_out, or_10_out, or_11_out, or_12_out, or_13_out,
       or_14_out, or_15_out, or_16_out, or_17_out, or_18_out, or_19_out, or_20_out, or_21_out, or_22_out,
       or_23_out, or_24_out, or_25_out, or_26_out, or_27_out, or_28_out, or_29_out, or_30_out, or_31_out,
       or_32_out;

  not not_1 (not_1_out, in_1[0]);
  not not_2 (not_2_out, in_1[1]);
  not not_3 (not_3_out, in_1[2]);
  not not_4 (not_4_out, in_1[3]);
  and load1 (load1_out, in_1[0], LOAD);
  and load0 (load0_out, not_1_out, LOAD);
  and load1_2 (load1_2_out, in_1[1], LOAD);
  and u_inc (inc_out, out_6[0], INC);
  and load0_2 (load0_2_out, not_2_out, LOAD);
  and load1_3 (load1_3_out, in_1[2], LOAD);
  and inc_2 (inc_2_out, inc_out, out_6[1]);
  and load0_3 (load0_3_out, not_3_out, LOAD);
  and load1_4 (load1_4_out, in_1[3], LOAD);
  and inc_3 (inc_3_out, inc_2_out, out_6[2]);
  and load0_4 (load0_4_out, not_4_out, LOAD);
  or or_1 (or_1_out, load1_out, INC);
  J_K_Flip_Flop b0 (.J(or_1_out), .clk(CLK), .K(or_2_out), .Q(out_6[0]));  // open: Qn, preset, en, reset
  or or_2 (or_2_out, INC, load0_out, CLR);
  or or_3 (or_3_out, load1_2_out, inc_out);
  J_K_Flip_Flop b1 (.J(or_3_out), .clk(CLK), .K(or_4_out), .Q(out_6[1]));  // open: Qn, preset, en, reset
  or or_4 (or_4_out, inc_out, load0_2_out, CLR);
  or or_5 (or_5_out, load1_3_out, inc_2_out);
  J_K_Flip_Flop b2 (.J(or_5_out), .clk(CLK), .K(or_6_out), .Q(out_6[2]));  // open: Qn, preset, en, reset
  or or_6 (or_6_out, inc_2_out, load0_3_out, CLR);
  or or_7 (or_7_out, load1_4_out, inc_3_out);
  J_K_Flip_Flop b3 (.J(or_7_out), .clk(CLK), .K(or_8_out), .Q(out_6[3]));  // open: Qn, preset, en, reset
  or or_8 (or_8_out, inc_3_out, load0_4_out, CLR);
  not not_5 (not_5_out, in_1[4]);
  not not_6 (not_6_out, in_1[5]);
  not not_7 (not_7_out, in_1[6]);
  not not_8 (not_8_out, in_1[7]);
  and and_1 (and_1_out, in_1[4], LOAD);
  and and_2 (and_2_out, inc_3_out, out_6[3]);
  and and_3 (and_3_out, not_5_out, LOAD);
  and and_4 (and_4_out, in_1[5], LOAD);
  and and_5 (and_5_out, and_2_out, out_6[4]);
  and and_6 (and_6_out, not_6_out, LOAD);
  and and_7 (and_7_out, in_1[6], LOAD);
  and and_8 (and_8_out, and_5_out, out_6[5]);
  and and_9 (and_9_out, not_7_out, LOAD);
  and and_10 (and_10_out, in_1[7], LOAD);
  and and_11 (and_11_out, and_8_out, out_6[6]);
  and and_12 (and_12_out, not_8_out, LOAD);
  or or_9 (or_9_out, and_1_out, and_2_out);
  or or_10 (or_10_out, and_2_out, and_3_out, CLR);
  or or_11 (or_11_out, and_4_out, and_5_out);
  or or_12 (or_12_out, and_5_out, and_6_out, CLR);
  or or_13 (or_13_out, and_7_out, and_8_out);
  or or_14 (or_14_out, and_8_out, and_9_out, CLR);
  or or_15 (or_15_out, and_10_out, and_11_out);
  or or_16 (or_16_out, and_11_out, and_12_out, CLR);
  J_K_Flip_Flop b4 (.J(or_9_out), .clk(CLK), .K(or_10_out), .Q(out_6[4]));  // open: Qn, preset, en, reset
  J_K_Flip_Flop b5 (.J(or_11_out), .clk(CLK), .K(or_12_out), .Q(out_6[5]));  // open: Qn, preset, en, reset
  J_K_Flip_Flop b6 (.J(or_13_out), .clk(CLK), .K(or_14_out), .Q(out_6[6]));  // open: Qn, preset, en, reset
  J_K_Flip_Flop b7 (.J(or_15_out), .clk(CLK), .K(or_16_out), .Q(out_6[7]));  // open: Qn, preset, en, reset
  not not_9 (not_9_out, in_1[8]);
  not not_10 (not_10_out, in_1[9]);
  not not_11 (not_11_out, in_1[10]);
  not not_12 (not_12_out, in_1[11]);
  and and_13 (and_13_out, in_1[8], LOAD);
  and and_14 (and_14_out, and_11_out, out_6[7]);
  and and_15 (and_15_out, not_9_out, LOAD);
  and and_16 (and_16_out, in_1[9], LOAD);
  and and_17 (and_17_out, and_14_out, out_6[8]);
  and and_18 (and_18_out, not_10_out, LOAD);
  and and_19 (and_19_out, in_1[10], LOAD);
  and and_20 (and_20_out, and_17_out, out_6[9]);
  and and_21 (and_21_out, not_11_out, LOAD);
  and and_22 (and_22_out, in_1[11], LOAD);
  and and_23 (and_23_out, and_20_out, out_6[10]);
  and and_24 (and_24_out, not_12_out, LOAD);
  or or_17 (or_17_out, and_13_out, and_14_out);
  or or_18 (or_18_out, and_14_out, and_15_out, CLR);
  or or_19 (or_19_out, and_16_out, and_17_out);
  or or_20 (or_20_out, and_17_out, and_18_out, CLR);
  or or_21 (or_21_out, and_19_out, and_20_out);
  or or_22 (or_22_out, and_20_out, and_21_out, CLR);
  or or_23 (or_23_out, and_22_out, and_23_out);
  or or_24 (or_24_out, and_23_out, and_24_out, CLR);
  J_K_Flip_Flop b4_2 (.J(or_17_out), .clk(CLK), .K(or_18_out), .Q(out_6[8]));  // open: Qn, preset, en, reset
  J_K_Flip_Flop b5_2 (.J(or_19_out), .clk(CLK), .K(or_20_out), .Q(out_6[9]));  // open: Qn, preset, en, reset
  J_K_Flip_Flop b6_2 (.J(or_21_out), .clk(CLK), .K(or_22_out), .Q(out_6[10]));  // open: Qn, preset, en, reset
  J_K_Flip_Flop b7_2 (.J(or_23_out), .clk(CLK), .K(or_24_out), .Q(out_6[11]));  // open: Qn, preset, en, reset
  not not_13 (not_13_out, in_1[12]);
  not not_14 (not_14_out, in_1[13]);
  not not_15 (not_15_out, in_1[14]);
  not not_16 (not_16_out, in_1[15]);
  and and_25 (and_25_out, in_1[12], LOAD);
  and and_26 (and_26_out, and_23_out, out_6[11]);
  and and_27 (and_27_out, not_13_out, LOAD);
  and and_28 (and_28_out, in_1[13], LOAD);
  and and_29 (and_29_out, and_26_out, out_6[12]);
  and and_30 (and_30_out, not_14_out, LOAD);
  and and_31 (and_31_out, in_1[14], LOAD);
  and and_32 (and_32_out, and_29_out, out_6[13]);
  and and_33 (and_33_out, not_15_out, LOAD);
  and and_34 (and_34_out, in_1[15], LOAD);
  and and_35 (and_35_out, and_32_out, out_6[14]);
  and and_36 (and_36_out, not_16_out, LOAD);
  or or_25 (or_25_out, and_25_out, and_26_out);
  or or_26 (or_26_out, and_26_out, and_27_out, CLR);
  or or_27 (or_27_out, and_28_out, and_29_out);
  or or_28 (or_28_out, and_29_out, and_30_out, CLR);
  or or_29 (or_29_out, and_31_out, and_32_out);
  or or_30 (or_30_out, and_32_out, and_33_out, CLR);
  or or_31 (or_31_out, and_34_out, and_35_out);
  or or_32 (or_32_out, and_35_out, and_36_out, CLR);
  J_K_Flip_Flop b4_3 (.J(or_25_out), .clk(CLK), .K(or_26_out), .Q(out_6[12]));  // open: Qn, preset, en, reset
  J_K_Flip_Flop b5_3 (.J(or_27_out), .clk(CLK), .K(or_28_out), .Q(out_6[13]));  // open: Qn, preset, en, reset
  J_K_Flip_Flop b6_3 (.J(or_29_out), .clk(CLK), .K(or_30_out), .Q(out_6[14]));  // open: Qn, preset, en, reset
  J_K_Flip_Flop b7_3 (.J(or_31_out), .clk(CLK), .K(or_32_out), .Q(out_6[15]));  // open: Qn, preset, en, reset
endmodule

module RegisterDemo (
  output [3:0] out_1,
  output [15:0] out_2,
  output [15:0] out_3
);

  wire clock_1_out, decoder_1_out0, decoder_1_out1;

  Clock clock_1 (.out(clock_1_out));
  _4bitcounter SC (.CLK(clock_1_out), .INC(1'b1), .clr(decoder_1_out1), .t(out_1));
  Decoder #(.select(4)) decoder_1 (
    .out0(decoder_1_out0), .out1(decoder_1_out1), .sel(out_1));  // open: out2, out3, out4, out5, out6, out7, out8, out9, out10, out11, out12, out13, out14, out15, en
  _16_bit_register PC (.LOAD(1'b0), .INC(decoder_1_out0), .CLR(1'b0), .CLK(clock_1_out), .out_6(out_2));  // open: in_1
  _16_bit_register AR (
    .in_1(out_2), .LOAD(decoder_1_out0), .INC(1'b0), .CLR(decoder_1_out1), .CLK(clock_1_out), .out_6(out_3));
endmodule

module RAMDemo (
  output [3:0] out_1,
  output [15:0] out_2,
  output [15:0] out_3,
  output [15:0] out_4
);

  wire clock_1_out, decoder_1_out0, decoder_1_out1, decoder_1_out2;
  wire [15:0] ram_1_data;

  Clock clock_1 (.out(clock_1_out));
  _4bitcounter SC (.CLK(clock_1_out), .INC(1'b1), .clr(decoder_1_out2), .t(out_1));
  Decoder #(.select(4)) decoder_1 (
    .out0(decoder_1_out0), .out1(decoder_1_out1), .out2(decoder_1_out2), .sel(out_1));  // open: out3, out4, out5, out6, out7, out8, out9, out10, out11, out12, out13, out14, out15, en
  _16_bit_register PC (.LOAD(1'b0), .INC(decoder_1_out0), .CLR(1'b0), .CLK(clock_1_out), .out_6(out_2));  // open: in_1
  _16_bit_register AR (.in_1(out_2), .LOAD(decoder_1_out0), .INC(1'b0), .CLR(1'b0), .CLK(clock_1_out), .out_6(out_3));
  RAM #(.addrWidth(12), .dataWidth(16), .bus("separate")) ram_1 (
    .addr(out_3[11:0]), .din(ram_1_data), .data(ram_1_data));  // open: str, sel, clk, ld, clr
  _16_bit_register IR (
    .in_1(ram_1_data), .LOAD(decoder_1_out1), .INC(1'b0), .CLR(1'b0), .CLK(clock_1_out), .out_6(out_4));
endmodule

module BusFor8 (
  input  s2,
  input  s1,
  input  s0,
  input  [15:0] RAM,
  input  [15:0] PC,
  input  [15:0] AR,
  input  [15:0] IR,
  input  [15:0] AC,
  input  [15:0] DR,
  input  [15:0] TR,
  output [15:0] out_11
);

  Multiplexer #(.select(3), .width(16)) multiplexer_1 (
    .in0(RAM), .in1(PC), .in2(AR), .in3(IR), .in4(AC), .in5(DR), .in6(TR), .in7({4'b0000, IR[11:0]}),
    .out(out_11), .sel({s2, s1, s0}));  // open: en
endmodule

module BusSimulation (
  output [3:0] out_1
);

  wire clock_1_out, decoder_1_out0, decoder_1_out1, decoder_1_out2;
  wire [15:0] AC_out_6, AR_out_6, busfor8_1_out_11, DR_out_6, IR_out_6, PC_out_6, ram_1_data, TR_out_6;

  Clock clock_1 (.out(clock_1_out));
  _4bitcounter SC (.CLK(clock_1_out), .INC(1'b1), .clr(decoder_1_out2), .t(out_1));
  RAM #(.addrWidth(12), .dataWidth(16), .bus("separate")) ram_1 (
    .din(busfor8_1_out_11), .data(ram_1_data), .clk(clock_1_out), .ld(decoder_1_out1));  // open: addr, str, sel, clr
  _16_bit_register PC (
    .in_1(busfor8_1_out_11), .INC(decoder_1_out0), .CLK(clock_1_out), .out_6(PC_out_6));  // open: LOAD, CLR
  _16_bit_register AR (
    .in_1(busfor8_1_out_11), .LOAD(decoder_1_out0), .CLK(clock_1_out), .out_6(AR_out_6));  // open: INC, CLR
  _16_bit_register IR (
    .in_1(busfor8_1_out_11), .LOAD(decoder_1_out1), .CLK(clock_1_out), .out_6(IR_out_6));  // open: INC, CLR
  _16_bit_register AC (.in_1(busfor8_1_out_11), .CLK(clock_1_out), .out_6(AC_out_6));  // open: LOAD, INC, CLR
  _16_bit_register DR (.in_1(busfor8_1_out_11), .CLK(clock_1_out), .out_6(DR_out_6));  // open: LOAD, INC, CLR
  _16_bit_register TR (.in_1(busfor8_1_out_11), .CLK(clock_1_out), .out_6(TR_out_6));  // open: LOAD, INC, CLR
  Decoder #(.select(4)) decoder_1 (
    .out0(decoder_1_out0), .out1(decoder_1_out1), .out2(decoder_1_out2), .sel(out_1));  // open: out3, out4, out5, out6, out7, out8, out9, out10, out11, out12, out13, out14, out15, en
  BusFor8 busfor8_1 (
    .RAM(ram_1_data), .PC(PC_out_6), .AR(AR_out_6), .IR(IR_out_6), .AC(AC_out_6), .DR(DR_out_6),
    .TR(TR_out_6), .s2(1'b0), .s1(decoder_1_out0), .s0(decoder_1_out0), .out_11(busfor8_1_out_11));
endmodule

// control logic
module CtrlLogic (
  input  [11:0] data,
  input  t5,
  input  t4,
  input  t3,
  input  t2,
  input  t1,
  input  t0,
  input  D7,
  input  D6,
  input  D5,
  input  D4,
  input  D3,
  input  D2,
  input  D1,
  input  D0,
  input  I,
  input  [15:0] AC,
  input  [15:0] DR,
  output [2:0] s,
  output PC_INC,
  output AC_INC,
  output MEM_RD,
  output MEM_WR,
  output AR_LD,
  output PC_LD,
  output IR_LD,
  output HLT,
  output AC_LD,
  output SC_CLR,
  output DR_LD,
  output [15:0] DR_2
);

  wire AC_0, and_1_out, and_2_out, and_3_out, and_4_out, and_10_out, and_11_out, and_12_out, and_13_out,
       and_14_out, and_15_out, and_16_out, and_17_out, I_prime, or_1_out, or_2_out, or_6_out, or_10_out;

  not not_1 (I_prime, I);
  nor nor_1 (AC_0, AC[8], AC[15], AC[14], AC[13], AC[12], AC[11], AC[10], AC[9], AC[7], AC[6], AC[5], AC[4], AC[3], AC[2], AC[1], AC[0]);
  and and_1 (and_1_out, t3, D7, data[2], AC_0);
  and and_2 (and_2_out, t3, or_1_out);
  or or_1 (or_1_out, D2, D3, D4);
  and and_3 (and_3_out, t3, I_prime);
  or or_2 (or_2_out, and_3_out, and_4_out);
  and and_4 (and_4_out, t4, I);
  or or_3 (PC_INC, t0, and_1_out);
  and and_5 (AC_INC, t3, D7, data[5]);
  or or_4 (MEM_RD, t1, and_2_out);
  and and_6 (MEM_WR, t3, D3);
  or or_5 (AR_LD, t0, t2);
  and and_7 (PC_LD, t3, D4);
  and and_8 (AC_LD, or_2_out, D2);
  and and_9 (DR_LD, t3, D2, I);
  and and_10 (and_10_out, D2, t4);
  and and_11 (and_11_out, t4, D2, I);
  and and_12 (and_12_out, t3, D2, I_prime);
  or or_6 (or_6_out, D3, D4, D7, and_16_out);
  or or_7 (SC_CLR, and_10_out, and_17_out);
  and and_13 (and_13_out, t4, D2);
  or or_8 (s[0], and_13_out, t0, t2);
  or or_9 (s[1], t2, and_14_out);
  and and_14 (and_14_out, t3, D4);
  or or_10 (or_10_out, and_11_out, and_12_out);
  or or_11 (s[2], or_10_out, t2, and_15_out);
  and and_15 (and_15_out, t3, D3);
  and and_16 (and_16_out, D2, I_prime);
  and and_17 (and_17_out, or_6_out, t3);
  and and_18 (HLT, data[0], D7);

  assign DR_2 = DR;
  assign IR_LD = t1;

  // Other names for the same wires on the sheet: B0 = data[0]; B2 = data[2]; B5 = data[5]
endmodule

// ins decode
module InstructionDecoder (
  input  [15:0] instruction,
  output [11:0] data,
  output D7,
  output D6,
  output D5,
  output D4,
  output D3,
  output D2,
  output D1,
  output D0,
  output I
);

  Decoder #(.select(3)) decoder_1 (
    .out0(D0), .out1(D1), .out2(D2), .out3(D3), .out4(D4), .out5(D5), .out6(D6), .out7(D7),
    .sel(instruction[14:12]));  // open: en

  assign data = instruction[11:0];
  assign I = instruction[15];
endmodule

module FINAL_CPU (
  output [2:0] out_1,
  output [3:0] out_2,
  output [15:0] Bus,
  output [15:0] PC,
  output [15:0] AR,
  output [15:0] IR,
  output [15:0] AC,
  output [15:0] DR
);

  wire and_1_out, clock_1_out, ctrllogic_1_ac_inc, ctrllogic_1_ac_ld, ctrllogic_1_ar_ld, ctrllogic_1_dr_ld,
       ctrllogic_1_ir_ld, ctrllogic_1_mem_rd, ctrllogic_1_mem_wr, ctrllogic_1_pc_inc, ctrllogic_1_pc_ld,
       ctrllogic_1_sc_clr, instructiondecoder_1_d0, instructiondecoder_1_d1, instructiondecoder_1_d2,
       instructiondecoder_1_d3, instructiondecoder_1_d4, instructiondecoder_1_d5, instructiondecoder_1_d6,
       instructiondecoder_1_d7, instructiondecoder_1_i, not_1_out, not_2_out, S, timedecoder_1_t0,
       timedecoder_1_t1, timedecoder_1_t2, timedecoder_1_t3, timedecoder_1_t4, timedecoder_1_t5;
  wire [11:0] instructiondecoder_1_data;
  wire [15:0] ctrllogic_1_dr_2, ram_1_data, TR_out_6;

  Clock clock_1 (.out(clock_1_out));
  not not_1 (not_1_out, S);
  and and_1 (and_1_out, clock_1_out, not_1_out);
  not not_2 (not_2_out, S);
  _4bitcounter u_4bitcounter_1 (.CLK(and_1_out), .INC(not_2_out), .clr(ctrllogic_1_sc_clr), .t(out_2));
  InstructionDecoder instructiondecoder_1 (
    .instruction(IR), .data(instructiondecoder_1_data), .D7(instructiondecoder_1_d7),
    .D6(instructiondecoder_1_d6), .D5(instructiondecoder_1_d5), .D4(instructiondecoder_1_d4),
    .D3(instructiondecoder_1_d3), .D2(instructiondecoder_1_d2), .D1(instructiondecoder_1_d1),
    .D0(instructiondecoder_1_d0), .I(instructiondecoder_1_i));
  TimeDecoder timedecoder_1 (
    .SC(out_2), .t5(timedecoder_1_t5), .t4(timedecoder_1_t4), .t3(timedecoder_1_t3), .t2(timedecoder_1_t2),
    .t1(timedecoder_1_t1), .t0(timedecoder_1_t0));
  CtrlLogic ctrllogic_1 (
    .data(instructiondecoder_1_data), .D7(instructiondecoder_1_d7), .D6(instructiondecoder_1_d6),
    .D5(instructiondecoder_1_d5), .D4(instructiondecoder_1_d4), .D3(instructiondecoder_1_d3),
    .D2(instructiondecoder_1_d2), .D1(instructiondecoder_1_d1), .D0(instructiondecoder_1_d0),
    .I(instructiondecoder_1_i), .AC(AC), .DR(DR), .t5(timedecoder_1_t5), .t4(timedecoder_1_t4),
    .t3(timedecoder_1_t3), .t2(timedecoder_1_t2), .t1(timedecoder_1_t1), .t0(timedecoder_1_t0),
    .SC_CLR(ctrllogic_1_sc_clr), .HLT(S), .s(out_1), .PC_INC(ctrllogic_1_pc_inc),
    .AC_INC(ctrllogic_1_ac_inc), .MEM_RD(ctrllogic_1_mem_rd), .MEM_WR(ctrllogic_1_mem_wr),
    .AR_LD(ctrllogic_1_ar_ld), .PC_LD(ctrllogic_1_pc_ld), .IR_LD(ctrllogic_1_ir_ld),
    .AC_LD(ctrllogic_1_ac_ld), .DR_LD(ctrllogic_1_dr_ld), .DR_2(ctrllogic_1_dr_2));
  RAM #(.addrWidth(12), .dataWidth(16), .bus("separate")) ram_1 (
    .addr(AR[11:0]), .din(Bus), .data(ram_1_data), .str(ctrllogic_1_mem_wr), .clk(and_1_out),
    .ld(ctrllogic_1_mem_rd));  // open: sel, clr
  _16_bit_register u_PC (
    .in_1(Bus), .LOAD(ctrllogic_1_pc_ld), .INC(ctrllogic_1_pc_inc), .CLR(1'b0), .CLK(and_1_out), .out_6(PC));
  _16_bit_register u_AR (.in_1(Bus), .LOAD(ctrllogic_1_ar_ld), .INC(1'b0), .CLR(1'b0), .CLK(and_1_out), .out_6(AR));
  _16_bit_register u_IR (.in_1(Bus), .LOAD(ctrllogic_1_ir_ld), .INC(1'b0), .CLR(1'b0), .CLK(and_1_out), .out_6(IR));
  _16_bit_register u_AC (
    .in_1(ctrllogic_1_dr_2), .LOAD(ctrllogic_1_ac_ld), .INC(ctrllogic_1_ac_inc), .CLR(1'b0), .CLK(and_1_out),
    .out_6(AC));
  _16_bit_register u_DR (.in_1(Bus), .LOAD(ctrllogic_1_dr_ld), .INC(1'b0), .CLR(1'b0), .CLK(and_1_out), .out_6(DR));
  _16_bit_register TR (.in_1(Bus), .LOAD(1'b0), .INC(1'b0), .CLR(1'b0), .CLK(and_1_out), .out_6(TR_out_6));
  BusFor8 busfor8_1 (
    .RAM(ram_1_data), .PC(PC), .AR(AR), .IR(IR), .AC(AC), .DR(DR), .TR(TR_out_6), .s2(out_1[2]),
    .s1(out_1[1]), .s0(out_1[0]), .out_11(Bus));

  // Notes on the sheet:
  //   Roope Rajala
  //   Peetu Nuottajärvi
  //   Samuel Savikoski
endmodule

// t dec
module TimeDecoder (
  input  [3:0] SC,
  output t5,
  output t4,
  output t3,
  output t2,
  output t1,
  output t0
);

  Decoder #(.select(4)) decoder_1 (
    .out0(t0), .out1(t1), .out2(t2), .out3(t3), .out4(t4), .out5(t5), .sel(SC));  // open: out6, out7, out8, out9, out10, out11, out12, out13, out14, out15, en
endmodule
